// Logisim project computer.circ as structural Verilog: 13 circuits, main circuit main
module main (
);

  wire A_IN, A_OUT, ACC_IN, ACC_OUT, ADDR_IN, ADRB_TO_MAR, alu_1_c, alu_1_z, and_1_out, ARG_IN, ARG_OUT,
       B_IN, B_OUT, CLK, comparator_1_eq, comparator_2_eq, COUNT, flag_1_c_out, flag_1_z_out, FLAG_IN, HALT,
       JUMP, LATCH_ACC, MAR_TO_ADRB, OP_IN, OUTPUT, PAGE_IN, PC_ADDR_OUT, PC_OUT, PC_PAGE_OUT, RAM_IN,
       RAM_OUT, RESET, SPTR_DECR, SPTR_IN, SPTR_INCR, SPTR_OUT, SUB, SUM_TO_ACC;
  wire [3:0] mar_1_a_out, mar_1_a_out_2, mar_1_a_out_3, mar_1_a_out_4, output_1_high, output_1_low,
       \µ_code_step_1_step ;
  wire [6:0] cir_1_op;
  wire [7:0] alu_1_d_out;
  wire [15:0] pc_1_monitor, stack_ptr_1_monitor;
  wire [15:5] decoder_1_data_out;
  wire [15:6] decoder_1_data_in;
  wire [21:16] decoder_1_ctrl;

  Button button_1 (.out(RESET));
  clock clock_1 (.HALT(HALT), .CLK(CLK));
  mar mar_1 (
    .CLK(CLK), .A_IN({mar_1_a_out_4, mar_1_a_out_3, mar_1_a_out_2, mar_1_a_out}), .D(alu_1_d_out),
    .A_OUT({mar_1_a_out_4, mar_1_a_out_3, mar_1_a_out_2, mar_1_a_out}), .ADDR_IN(ADDR_IN),
    .FROM_ADRB(ADRB_TO_MAR), .TO_ADRB(MAR_TO_ADRB), .PAGE_IN(PAGE_IN), .RESET(RESET));
  alu alu_1 (
    .D_IN(alu_1_d_out), .LATCH_ACC(LATCH_ACC), .SUB(SUB), .SUM__ACC(SUM_TO_ACC), .Z(alu_1_z),
    .ACC_IN(ACC_IN), .ACC_OUT(ACC_OUT), .D_OUT(alu_1_d_out), .CLK(CLK), .C(alu_1_c), .RESET(RESET));
  // Probe on {mar_1_a_out_4, mar_1_a_out_3, mar_1_a_out_2, mar_1_a_out}
  // Probe on alu_1_d_out
  // Probe on pc_1_monitor
  flag flag_1 (
    .Z_IN(alu_1_z), .C_IN(alu_1_c), .LOAD(FLAG_IN), .Z_OUT(flag_1_z_out), .C_OUT(flag_1_c_out), .CLK(CLK),
    .RESET(RESET));
  Hex_Digit_Display hex_digit_display_1 (.value(mar_1_a_out_4));  // open: dp
  Hex_Digit_Display hex_digit_display_2 (.value(mar_1_a_out_3));  // open: dp
  Hex_Digit_Display hex_digit_display_3 (.value(alu_1_d_out[3:0]));  // open: dp
  Hex_Digit_Display hex_digit_display_4 (.value(alu_1_d_out[7:4]));  // open: dp
  register A (.D_IN(alu_1_d_out), .CLK(CLK), .D_OUT(alu_1_d_out), .IN(A_IN), .OUT(A_OUT), .RESET(RESET));
  register B (.D_IN(alu_1_d_out), .CLK(CLK), .D_OUT(alu_1_d_out), .IN(B_IN), .OUT(B_OUT), .RESET(RESET));
  ram ram_1 (
    .OUT(RAM_OUT), .D_OUT(alu_1_d_out), .A({mar_1_a_out_4, mar_1_a_out_3, mar_1_a_out_2, mar_1_a_out}),
    .D_IN(alu_1_d_out), .IN(RAM_IN));
  pc pc_1 (
    .JUMP(JUMP), .A_IN({mar_1_a_out_4, mar_1_a_out_3, mar_1_a_out_2, mar_1_a_out}), .COUNT(COUNT),
    .A_OUT({mar_1_a_out_4, mar_1_a_out_3, mar_1_a_out_2, mar_1_a_out}), .CLK(CLK), .OUT(PC_OUT),
    .MONITOR(pc_1_monitor), .RESET(RESET), .D_OUT(alu_1_d_out), .ADDR_OUT(PC_ADDR_OUT), .PAGE_OUT(PC_PAGE_OUT));
  cir cir_1 (
    .OP_IN(OP_IN), .D_IN(alu_1_d_out), .D_OUT(alu_1_d_out), .OP(cir_1_op), .CLK(CLK), .ARG_OUT(ARG_OUT),
    .ARG_IN(ARG_IN), .RESET(RESET));
  \µ_code_step  \u_µ_code_step_1  (.CLK(CLK), .STEP(\µ_code_step_1_step ), .RESET(RESET), ._0(and_1_out));
  // Probe on \µ_code_step_1_step 
  and and_1 (and_1_out, comparator_2_eq, comparator_1_eq);
  Hex_Digit_Display hex_digit_display_5 (.value(mar_1_a_out_2));  // open: dp
  Hex_Digit_Display hex_digit_display_6 (.value(mar_1_a_out));  // open: dp
  // Probe on cir_1_op
  decoder decoder_1 (
    .STEP(\µ_code_step_1_step ), .C(flag_1_c_out), .Z(flag_1_z_out), .OP(cir_1_op),
    .DATA_OUT({decoder_1_data_out[15:8], PC_PAGE_OUT, PC_ADDR_OUT, decoder_1_data_out[5], ARG_OUT, ACC_OUT, RAM_OUT, B_OUT, A_OUT}),
    .DATA_IN({decoder_1_data_in[15:9], OUTPUT, decoder_1_data_in[7:6], OP_IN, ARG_IN, ACC_IN, RAM_IN, B_IN, A_IN}),
    .CTRL({decoder_1_ctrl, HALT, COUNT, SPTR_DECR, SPTR_INCR, SPTR_OUT, SPTR_IN, PC_OUT, JUMP, SUM_TO_ACC, LATCH_ACC, FLAG_IN, SUB, ADRB_TO_MAR, MAR_TO_ADRB, ADDR_IN, PAGE_IN}));
  stack_ptr stack_ptr_1 (
    .MONITOR(stack_ptr_1_monitor), .SET(SPTR_IN),
    .A_IN({mar_1_a_out_4, mar_1_a_out_3, mar_1_a_out_2, mar_1_a_out}),
    .A_OUT({mar_1_a_out_4, mar_1_a_out_3, mar_1_a_out_2, mar_1_a_out}), .RESET(RESET), .INCR(SPTR_INCR),
    .OUT(SPTR_OUT), .CLK(CLK), .DECR(SPTR_DECR));
  Comparator #(.width(22), .mode("unsigned")) comparator_1 (
    .a({decoder_1_ctrl, HALT, COUNT, SPTR_DECR, SPTR_INCR, SPTR_OUT, SPTR_IN, PC_OUT, JUMP, SUM_TO_ACC, LATCH_ACC, FLAG_IN, SUB, ADRB_TO_MAR, MAR_TO_ADRB, ADDR_IN, PAGE_IN}),
    .b({22{1'b0}}), .eq(comparator_1_eq));  // open: gt, lt
  Hex_Digit_Display hex_digit_display_7 (.value(output_1_high));  // open: dp
  Hex_Digit_Display hex_digit_display_8 (.value(output_1_low));  // open: dp
  \output  output_1 (.D(alu_1_d_out), .IN(OUTPUT), .CLK(CLK), .RESET(RESET), .LOW(output_1_low), .HIGH(output_1_high));
  // Probe on stack_ptr_1_monitor
  Comparator #(.width(32), .mode("unsigned")) comparator_2 (
    .a({decoder_1_data_in[15:9], OUTPUT, decoder_1_data_in[7:6], OP_IN, ARG_IN, ACC_IN, RAM_IN, B_IN, A_IN, decoder_1_data_out[15:8], PC_PAGE_OUT, PC_ADDR_OUT, decoder_1_data_out[5], ARG_OUT, ACC_OUT, RAM_OUT, B_OUT, A_OUT}),
    .b({32{1'b0}}), .eq(comparator_2_eq));  // open: gt, lt

  // Notes on the sheet:
  //   Memory Address Register
  //   Clock
  //   Arithmetic + Logic Unit
  //   Address Bus
  //   Data Bus
  //   A Register
  //   B Register
  //   Memory
  //   Program Counter
  //   Current
  //   Instruction
  //   Register
  //   Instruction Decoder
  //   Microcode
  //   Output
  //   Stack Pointer
  //   Resetter
endmodule

// REG
module register (
  input  [7:0] D_IN,
  input  IN,
  input  OUT,
  input  CLK,
  input  RESET,
  output [7:0] D_OUT
);

  wire not_1_out;
  wire [7:0] register_1_q;

  not not_1 (not_1_out, CLK);
  assign D_OUT = OUT ? register_1_q : 8'bz;  // Controlled_Buffer controlled_buffer_1
  Register register_1 (.D(D_IN), .en(IN), .Q(register_1_q), .clk(not_1_out), .clr(RESET));
endmodule

// RAM
module ram (
  input  OUT,
  input  [15:0] A,
  input  [7:0] D_IN,
  input  IN,
  output [7:0] D_OUT
);

  wire or_1_out;
  wire [7:0] ram_1_data;

  or or_1 (or_1_out, OUT, IN);
  RAM #(.addrWidth(16), .bus("asynch")) ram_1 (.addr(A), .data(ram_1_data), .sel(or_1_out), .ld(OUT));  // open: clr
  assign D_OUT = OUT ? ram_1_data : 8'bz;  // Controlled_Buffer controlled_buffer_1
  assign ram_1_data = IN ? D_IN : 8'bz;  // Controlled_Buffer controlled_buffer_2
endmodule

// MAR
module mar (
  input  CLK,
  input  [15:0] A_IN,
  input  [7:0] D,
  input  RESET,
  input  ADDR_IN,
  input  PAGE_IN,
  input  FROM_ADRB,
  input  TO_ADRB,
  output [15:0] A_OUT
);

  wire or_1_out, or_2_out;
  wire [7:0] multiplexer_1_out, multiplexer_2_out;

  Multiplexer #(.width(8), .enable("false")) multiplexer_1 (
    .in0(A_IN[7:0]), .in1(D), .out(multiplexer_1_out), .sel(ADDR_IN));
  register ADDR (.D_IN(multiplexer_1_out), .CLK(CLK), .D_OUT(A_OUT[7:0]), .IN(or_1_out), .OUT(TO_ADRB), .RESET(RESET));
  or or_1 (or_1_out, ADDR_IN, FROM_ADRB);
  register PAGE (.D_IN(multiplexer_2_out), .CLK(CLK), .D_OUT(A_OUT[15:8]), .IN(or_2_out), .OUT(TO_ADRB), .RESET(RESET));
  Multiplexer #(.width(8), .enable("false")) multiplexer_2 (
    .in0(A_IN[15:8]), .in1(D), .out(multiplexer_2_out), .sel(PAGE_IN));
  or or_2 (or_2_out, PAGE_IN, FROM_ADRB);
endmodule

// ALU
module alu (
  input  [7:0] D_IN,
  input  LATCH_ACC,
  input  SUB,
  input  CLK,
  input  SUM__ACC,
  input  RESET,
  input  ACC_IN,
  input  ACC_OUT,
  output C,
  output Z,
  output [7:0] D_OUT
);

  wire nor_1_out, nor_2_out, nor_3_out, nor_4_out, not_1_out, not_2_out, or_1_out;
  wire [7:0] Accumulator_q, adder_1_out, bit_extender_1_out, Latch_q, multiplexer_1_out, xor_1_out;

  Multiplexer #(.width(8), .enable("false")) multiplexer_1 (
    .in0(D_IN), .in1(adder_1_out), .out(multiplexer_1_out), .sel(SUM__ACC));
  or or_1 (or_1_out, SUM__ACC, ACC_IN);
  Register Accumulator (.D(multiplexer_1_out), .en(or_1_out), .Q(Accumulator_q), .clk(not_1_out), .clr(RESET));
  not not_1 (not_1_out, CLK);
  not not_2 (not_2_out, CLK);
  assign D_OUT = ACC_OUT ? Accumulator_q : 8'bz;  // Controlled_Buffer controlled_buffer_1
  Register Latch (.D(Accumulator_q), .en(LATCH_ACC), .Q(Latch_q), .clk(not_2_out), .clr(RESET));
  and and_1 (Z, nor_1_out, nor_2_out, nor_3_out, nor_4_out);
  assign bit_extender_1_out = {{7{SUB}}, SUB};  // Bit_Extender bit_extender_1
  nor nor_1 (nor_1_out, adder_1_out[0], adder_1_out[1]);
  nor nor_2 (nor_2_out, adder_1_out[2], adder_1_out[3]);
  nor nor_3 (nor_3_out, adder_1_out[4], adder_1_out[5]);
  nor nor_4 (nor_4_out, adder_1_out[6], adder_1_out[7]);
  assign xor_1_out = bit_extender_1_out ^ D_IN;  // XOR_Gate xor_1, 8 bits wide
  Adder adder_1 (.a(Latch_q), .b(xor_1_out), .out(adder_1_out), .cin(SUB), .cout(C));
  // Probe on adder_1_out
endmodule

// FLAG
module flag (
  input  Z_IN,
  input  C_IN,
  input  LOAD,
  input  CLK,
  input  RESET,
  output Z_OUT,
  output C_OUT
);

  wire not_1_out;

  Register #(.width(2)) register_1 (.D({C_IN, Z_IN}), .en(LOAD), .Q({C_OUT, Z_OUT}), .clk(not_1_out), .clr(RESET));
  not not_1 (not_1_out, CLK);
endmodule

// CLOCK
module clock (
  input  HALT,
  output CLK
);

  wire clock_1_out, not_1_out;

  Clock clock_1 (.out(clock_1_out));
  and and_1 (CLK, clock_1_out, not_1_out);
  not not_1 (not_1_out, HALT);
endmodule

// PC
module pc (
  input  ADDR_OUT,
  input  PAGE_OUT,
  input  JUMP,
  input  [15:0] A_IN,
  input  RESET,
  input  COUNT,
  input  OUT,
  input  CLK,
  output [7:0] D_OUT,
  output [15:0] MONITOR,
  output [15:0] A_OUT
);

  wire or_1_out, xor_1_out;

  Counter #(.width(16), .max('hffff)) counter_1 (
    .load(JUMP), .D(A_IN), .count(COUNT), .Q(MONITOR), .clk(xor_1_out), .clr(RESET));  // open: carry
  xor xor_1 (xor_1_out, JUMP, CLK);
  or or_1 (or_1_out, ADDR_OUT, PAGE_OUT);
  assign A_OUT = OUT ? MONITOR : 16'bz;  // Controlled_Buffer controlled_buffer_1
  Multiplexer #(.width(8)) multiplexer_1 (
    .in0(MONITOR[7:0]), .in1(MONITOR[15:8]), .out(D_OUT), .sel(PAGE_OUT), .en(or_1_out));
endmodule

// CIR
module cir (
  input  OP_IN,
  input  [7:0] D_IN,
  input  RESET,
  input  CLK,
  input  ARG_OUT,
  input  ARG_IN,
  output [6:0] OP,
  output [7:0] D_OUT
);

  wire [7:7] register_1_q;

  Register register_1 (.D(D_IN), .en(OP_IN), .Q({register_1_q[7], OP}), .clk(CLK), .clr(RESET));
  register ARG (.D_IN(D_IN), .CLK(CLK), .D_OUT(D_OUT), .IN(ARG_IN), .OUT(ARG_OUT), .RESET(RESET));
endmodule

// DEC
module decoder (
  input  [3:0] STEP,
  input  C,
  input  Z,
  input  [6:0] OP,
  output [21:0] CTRL,
  output [15:0] DATA_OUT,
  output [15:0] DATA_IN
);

  wire [9:0] rom_1_data;

  ROM #(.addrWidth(13), .dataWidth(32)) rom_1 (.addr({OP, Z, C, STEP}), .data({CTRL, rom_1_data}));  // open: sel
  Demultiplexer #(.select(4), .enable("false")) demultiplexer_1 (
    .out0(DATA_OUT[0]), .out1(DATA_OUT[1]), .out2(DATA_OUT[2]), .out3(DATA_OUT[3]), .out4(DATA_OUT[4]),
    .out5(DATA_OUT[5]), .out6(DATA_OUT[6]), .out7(DATA_OUT[7]), .out8(DATA_OUT[8]), .out9(DATA_OUT[9]),
    .out10(DATA_OUT[10]), .out11(DATA_OUT[11]), .out12(DATA_OUT[12]), .out13(DATA_OUT[13]),
    .out14(DATA_OUT[14]), .out15(DATA_OUT[15]), .in(rom_1_data[0]), .sel(rom_1_data[4:1]));
  Demultiplexer #(.select(4), .enable("false")) demultiplexer_2 (
    .out0(DATA_IN[0]), .out1(DATA_IN[1]), .out2(DATA_IN[2]), .out3(DATA_IN[3]), .out4(DATA_IN[4]),
    .out5(DATA_IN[5]), .out6(DATA_IN[6]), .out7(DATA_IN[7]), .out8(DATA_IN[8]), .out9(DATA_IN[9]),
    .out10(DATA_IN[10]), .out11(DATA_IN[11]), .out12(DATA_IN[12]), .out13(DATA_IN[13]), .out14(DATA_IN[14]),
    .out15(DATA_IN[15]), .in(rom_1_data[5]), .sel(rom_1_data[9:6]));

  // Notes on the sheet:
  //   contents of rom_1 (hex, n*v repeats v):
  //   140010 20000 440010 20000 80000 11*0 140010 20000 440010 20000 80000 11*0 140010 20000 440010 20000
  //   80000 11*0 140010 20000 440010 20000 80000 11*0 140010 20000 440010 20000 200080 8110 10*0 140010
  //   20000 440010 20000 200080 8110 10*0 140010 20000 440010 20000 200080 8110 10*0 140010 20000 440010
  //   20000 200080 8110 10*0 140010 20000 440010 20000 200080 4120 10*0 140010 20000 440010 20000 200080
  //   4120 10*0 140010 20000 440010 20000 200080 4120 10*0 140010 20000 440010 20000 200080 4120 10*0
  //   140010 20000 440010 20000 804000 11*0 140010 20000 440010 20000 804000 11*0 140010 20000 440010
  //   20000 804000 11*0 140010 20000 440010 20000 804000 11*0 140010 20000 440010 20000 12*0 140010 20000
  //   440010 20000 12*0 140010 20000 440010 20000 12*0 140010 20000 440010 20000 12*0 140010 20000 440010
  //   20000 200080 190 8110 9*0 140010 20000 440010 20000 200080 190 8110 9*0 140010 20000 440010 20000
  //   200080 190 8110 9*0 140010 20000 440010 20000 200080 190 8110 9*0 140010 20000 440010 20000 9 11*0
  //   140010 20000 440010 20000 9 11*0 140010 20000 440010 20000 9 11*0 140010 20000 440010 20000 9 11*0
  //   140010 20000 440010 20000 8001 11*0 140010 20000 440010 20000 8001 11*0 140010 20000 440010 20000
  //   8001 11*0 140010 20000 440010 20000 8001 11*0 140010 20000 440010 20000 81 8110 10*0 140010 20000
  //   440010 20000 81 8110 10*0 140010 20000 440010 20000 81 8110 10*0 140010 20000 440010 20000 81 8110
  //   10*0 140010 20000 440010 20000 6 11*0 140010 20000 440010 20000 6 11*0 140010 20000 440010 20000 6
  //   11*0 140010 20000 440010 20000 6 11*0 140010 20000 440010 20000 84 8110 10*0 140010 20000 440010
  //   20000 84 8110 10*0 140010 20000 440010 20000 84 8110 10*0 140010 20000 440010 20000 84 8110 10*0
  //   140010 20000 440010 20000 8004 11*0 140010 20000 440010 20000 8004 11*0 140010 20000 440010 20000
  //   8004 11*0 140010 20000 440010 20000 8004 11*0 140010 20000 440010 20000 200080 190 4120 9*0 140010
  //   20000 440010 20000 200080 190 4120 9*0 140010 20000 440010 20000 200080 190 4120 9*0 140010 20000
  //   440010 20000 200080 190 4120 9*0 140010 20000 440010 20000 4002 11*0 140010 20000 440010 20000 4002
  //   11*0 140010 20000 440010 20000 4002 11*0 140010 20000 440010 20000 4002 11*0 140010 20000 440010
  //   20000 4008 11*0 140010 20000 440010 20000 4008 11*0 140010 20000 440010 20000 4008 11*0 140010 20000
  //   440010 20000 4008 11*0 140010 20000 440010 20000 81 4120 10*0 140010 20000 440010 20000 81 4120 10*0
  //   140010 20000 440010 20000 81 4120 10*0 140010 20000 440010 20000 81 4120 10*0 140010 20000 440010
  //   20000 201080 2910 10*0 140010 20000 440010 20000 201080 2910 10*0 140010 20000 440010 20000 201080
  //   2910 10*0 140010 20000 440010 20000 201080 2910 10*0 140010 20000 440010 20000 1000 2801 10*0 140010
  //   20000 440010 20000 1000 2801 10*0 140010 20000 440010 20000 1000 2801 10*0 140010 20000 440010 20000
  //   1000 2801 10*0 140010 20000 440010 20000 1000 2804 10*0 140010 20000 440010 20000 1000 2804 10*0
  //   140010 20000 440010 20000 1000 2804 10*0 140010 20000 440010 20000 1000 2804 10*0 140010 20000
  //   440010 20000 84 4120 10*0 140010 20000 440010 20000 84 4120 10*0 140010 20000 440010 20000 84 4120
  //   10*0 140010 20000 440010 20000 84 4120 10*0 140010 20000 440010 20000 201080 2d10 10*0 140010 20000
  //   440010 20000 201080 2d10 10*0 140010 20000 440010 20000 201080 2d10 10*0 140010 20000 440010 20000
  //   201080 2d10 10*0 140010 20000 440010 20000 1000 2c01 10*0 140010 20000 440010 20000 1000 2c01 10*0
  //   140010 20000 440010 20000 1000 2c01 10*0 140010 20000 440010 20000 1000 2c01 10*0 140010 20000
  //   440010 20000 1000 2c04 10*0 140010 20000 440010 20000 1000 2c04 10*0 140010 20000 440010 20000 1000
  //   2c04 10*0 140010 20000 440010 20000 1000 2c04 10*0 140010 20000 440010 20000 200040 11*0 140010
  //   20000 440010 20000 200040 11*0 140010 20000 440010 20000 200040 11*0 140010 20000 440010 20000
  //   200040 11*0 140010 20000 440010 20000 200080 10100 10*0 140010 20000 440010 20000 200080 10100 10*0
  //   140010 20000 440010 20000 200080 10100 10*0 140010 20000 440010 20000 200080 10100 10*0 140010 20000
  //   440010 20000 12*0 140010 20000 440010 20000 12*0 140010 200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
endmodule

// STP
module \µ_code_step  (
  input  CLK,
  input  RESET,
  input  _0,
  output [3:0] STEP
);

  wire and_1_out, d_ff_1_q, not_1_out, or_1_out;

  not not_1 (not_1_out, CLK);
  D_Flip_Flop d_ff_1 (.clk(not_1_out), .D(1'b1), .Q(d_ff_1_q), .reset(RESET));  // open: Qn, preset, en
  and and_1 (and_1_out, d_ff_1_q, CLK);
  or or_1 (or_1_out, RESET, _0);
  Counter #(.width(4), .max('hf)) counter_1 (
    .count(1'b1), .Q(STEP), .clk(and_1_out), .clr(or_1_out));  // open: load, D, carry
endmodule

// OUT
module \output  (
  input  [7:0] D,
  input  IN,
  input  CLK,
  input  RESET,
  output [3:0] LOW,
  output [3:0] HIGH
);

  wire not_1_out;

  Register register_1 (.D(D), .en(IN), .Q({HIGH, LOW}), .clk(not_1_out), .clr(RESET));
  not not_1 (not_1_out, CLK);
endmodule

// STACK PTR
module stack_ptr (
  input  SET,
  input  [15:0] A_IN,
  input  RESET,
  input  INCR,
  input  DECR,
  input  OUT,
  input  CLK,
  output [15:0] MONITOR,
  output [15:0] A_OUT
);

  wire or_1_out, or_2_out, xor_1_out;

  or or_1 (or_1_out, SET, DECR);
  or or_2 (or_2_out, INCR, DECR);
  Counter #(.width(16), .max('hffff)) counter_1 (
    .load(or_1_out), .D(A_IN), .count(or_2_out), .Q(MONITOR), .clk(xor_1_out), .clr(RESET));  // open: carry
  xor xor_1 (xor_1_out, SET, CLK);
  assign A_OUT = OUT ? MONITOR : 16'bz;  // Controlled_Buffer controlled_buffer_1
endmodule
